// Digital circuit D 2_5.dig as structural Verilog
module D_2_5 (
  input  clk,
  input  reset,
  input  B,
  input  S,
  output L,
  output [2:0] States,
  output F,
  output H
);

  wire and_1_out, and_2_out, and_3_out, and_4_out, and_5_out, or_1_out, or_2_out, Q_0_t, Q_1_t, Q_2_t;

  and and_1 (and_1_out, Q_0_t, Q_1_t, S, Q_2_t);
  or or_1 (or_1_out, and_1_out, B);
  xor xor_1 (L, States[1], States[0]);
  D_FF_AS d_ff_as_1 (.Set(reset), .D(or_1_out), .C(clk), .Clr(1'b0), .Q(States[0]), .nQ(Q_2_t));
  and and_2 (and_2_out, ~B, L);  // And
  and and_3 (and_3_out, States[1], B, ~S);  // And
  and and_4 (and_4_out, States[1], B, States[0]);
  D_FF_AS d_ff_as_2 (.Set(1'b0), .D(or_2_out), .C(clk), .Clr(reset), .Q(States[1]), .nQ(Q_1_t));
  Demultiplexer demultiplexer_1 (.sel(States[1]), .in(States[0]), .out_0(H), .out_1(F));
  or or_2 (or_2_out, and_2_out, and_3_out, and_4_out);
  D_FF_AS d_ff_as_3 (.Set(1'b0), .D(and_5_out), .C(clk), .Clr(reset), .Q(States[2]), .nQ(Q_0_t));
  and and_5 (and_5_out, ~L, ~S, ~B);  // And

  // Other names for the same wires on the sheet: Q_0 = States[2]; Q_1 = States[1]; Q_2 = States[0]; rst = reset
endmodule
