// Digital circuit Testing.dig as structural Verilog
module Testing (
  input  [2:0] Q,
  input  [2:0] B,
  input  S,
  output [2:0] Q__plus
);

  wire and_1_out, and_2_out, nor_1_out, nor_2_out, nor_3_out, not_1_out, not_2_out, not_3_out, not_4_out;

  not not_1 (not_1_out, B[2]);
  not not_2 (not_2_out, B[2]);
  not not_3 (not_3_out, B[2]);
  not not_4 (not_4_out, B[2]);
  and and_1 (and_1_out, B[2], B[2], not_3_out);
  nor nor_1 (nor_1_out, not_2_out, B[2], B[2]);
  nor nor_2 (nor_2_out, B[2], B[2], B[2], not_4_out);
  xor xor_1 (Q__plus[1], B[2], B[2]);
  nor nor_3 (nor_3_out, B[2], B[2], B[2], B[2]);
  and and_2 (and_2_out, B[2], B[2], not_1_out);
  or or_1 (Q__plus[0], and_1_out, nor_1_out, nor_2_out);
  or or_2 (Q__plus[2], nor_3_out, and_2_out);
  // Pins of 1 and 3 bits meet at {3{B[2]}}

  assign B[1:0] = {2{B[2]}};
  assign S = B[2];
endmodule
