// Digital circuit D1 circuit.dig as structural Verilog
module D1_circuit (
  input  clk,
  input  reset,
  input  B,
  input  S,
  output [2:0] State,
  output L,
  output F,
  output H
);

  wire and_1_out, and_2_out, and_5_out, or_1_out, or_2_out, Q_0_t, Q_1_t, Q_2_t;

  and and_1 (and_1_out, Q_2_t, Q_1_t, ~S, ~B);  // And
  and and_2 (and_2_out, State[1], State[0], ~B);  // And
  or or_1 (or_1_out, and_1_out, and_2_out);
  D_FF_AS d_ff_as_1 (.Set(1'b0), .D(or_1_out), .C(clk), .Clr(reset), .Q(State[2]), .nQ(Q_0_t));
  xor xor_1 (L, State[1], State[0]);
  D_FF_AS d_ff_as_2 (.Set(1'b0), .D(L), .C(clk), .Clr(reset), .Q(State[1]), .nQ(Q_1_t));
  and and_3 (H, Q_1_t, State[0]);
  and and_4 (F, State[1], State[0]);
  and and_5 (and_5_out, S, Q_0_t, Q_2_t, Q_1_t);
  or or_2 (or_2_out, and_5_out, B);
  D_FF_AS d_ff_as_3 (.Set(reset), .D(or_2_out), .C(clk), .Clr(reset), .Q(State[0]), .nQ(Q_2_t));

  // Other names for the same wires on the sheet: Q_0 = State[2]; Q_1 = State[1]; Q_2 = State[0]; rst = reset
endmodule
