// Digital circuit DetailedMicroprocessor.dig as structural Verilog
module DetailedMicroprocessor (
  input  clk,
  input  [3:0] data__in,
  input  reset,
  output [3:0] accum
);

  wire not_1_out;
  wire [1:0] Step_Reg_q;
  wire [3:0] alu_1_p1, alu_1_p7, data__mux_y, four_bit_mux_1_y, Instruction_Reg_q, MAR_q, program__ram_d,
       program_ctr_1_q;
  wire [9:0] microcode_ROM_d;
  wire [13:10] microcode_ROM_d_2;

  four_bit_reg Instruction_Reg (
    .d(alu_1_p1), .enable(microcode_ROM_d[0]), .reset(reset), .clk(clk), .q(Instruction_Reg_q));
  program_ctr program_ctr_1 (.enable(microcode_ROM_d[9]), .reset(reset), .clk(clk), .q(program_ctr_1_q));
  four_bit_reg MAR (.d(alu_1_p1), .enable(microcode_ROM_d[8]), .reset(reset), .clk(clk), .q(MAR_q));
  not not_1 (not_1_out, microcode_ROM_d[9]);
  two_bit_reg Step_Reg (.d(microcode_ROM_d_2[13:12]), .enable(1'b1), .reset(reset), .clk(clk), .q(Step_Reg_q));
  four_bit_mux four_bit_mux_1 (.a(program_ctr_1_q), .b(MAR_q), .sel(not_1_out), .y(four_bit_mux_1_y));
  ROM #(.AddrBits(6), .Bits(14)) microcode_ROM (
    .A({Instruction_Reg_q, Step_Reg_q}), .sel(1'b1), .D({microcode_ROM_d_2, microcode_ROM_d}));
  // alu alu_1: pin names not known; wires that end beside it: alu_1_p1, accum, microcode_ROM_d[6], microcode_ROM_d[7], microcode_ROM_d[5], 1'b0, alu_1_p7
  four_bit_reg accumulator (.d(alu_1_p7), .enable(microcode_ROM_d[4]), .reset(reset), .clk(clk), .q(accum));
  four_bit_mux accum__mux (.a(data__mux_y), .b(accum), .sel(microcode_ROM_d[3]), .y(alu_1_p1));
  RAMDualPort #(.AddrBits(4), .isProgramMemory("true"), .Bits(4)) program__ram (
    .A(four_bit_mux_1_y), .Din(alu_1_p1), .str(microcode_ROM_d[1]), .C(clk), .ld(1'b1), .D(program__ram_d));
  four_bit_mux data__mux (.a(data__in), .b(program__ram_d), .sel(microcode_ROM_d[2]), .y(data__mux_y));

  // Notes on the sheet:
  //   contents of microcode_ROM (hex, n*v repeats v):
  //   1205,234,0,0,1205,294,0,0,1205,1000,0,0,1205,0,0,0,1205,0,0,0
  //   ,1205,0,0,0,1205,0,0,0,1205,0,0,3fff
endmodule
