// Digital circuit controller.dig as structural Verilog
module controller (
  input  clk,
  input  reset,
  input  [3:0] data__bus,
  input  load__ir,
  output [9:0] controler
);

  wire [1:0] step__reg;
  wire [3:0] instr__reg;
  wire [13:10] rom__out;

  four_bit_reg Instruction_Reg (.d(data__bus), .enable(load__ir), .reset(reset), .clk(clk), .q(instr__reg));
  two_bit_reg Step_Reg (.d(rom__out[13:12]), .enable(1'b1), .reset(reset), .clk(clk), .q(step__reg));
  ROM #(.AddrBits(6), .Bits(14)) microcode_ROM (.A({instr__reg, step__reg}), .sel(1'b1), .D({rom__out, controler}));

  // Other names for the same wires on the sheet: rom__out[9:0] = controler

  // Notes on the sheet:
  //   contents of microcode_ROM (hex, n*v repeats v):
  //   1205,234,0,0,1205,294,0,0,1205,1000,0,0,1205,0,0,0,1205,0,0,0
  //   ,1205,0,0,0,1205,0,0,0,1205,0,0,3fff
endmodule
