// Digital circuit incrementer.dig as structural Verilog
module incrementer (
  input  [3:0] a,
  input  inc,
  output cry,
  output [3:0] y
);

  wire half_adder_1_p2, half_adder_2_p2, half_adder_3_p2;

  // half_adder half_adder_1: pin names not known; wires that end beside it: a[3], half_adder_1_p2, y[3], cry
  // half_adder half_adder_2: pin names not known; wires that end beside it: a[2], half_adder_2_p2, y[2], half_adder_1_p2
  // half_adder half_adder_3: pin names not known; wires that end beside it: a[1], half_adder_3_p2, y[1], half_adder_2_p2
  // half_adder half_adder_4: pin names not known; wires that end beside it: a[0], inc, y[0], half_adder_3_p2
endmodule
