// Digital circuit brainless.dig as structural Verilog
module brainless (
  input  invert,
  input  arith,
  input  pass,
  input  load__acc,
  input  acc__to__db,
  input  reset,
  input  clk,
  input  write,
  input  read,
  input  [3:0] data__in,
  input  [3:0] addr__bus,
  output [3:0] alu__out,
  output [3:0] accum,
  output [3:0] data__bus
);

  wire [3:0] data__mux_y, program_ram_1_data__out;

  alu alu_1 (
    .a(data__bus), .b(accum), .invert(invert), .arith(arith), .pass(pass), .cin(1'b0), .y(alu__out));  // open: cout, overfl
  four_bit_reg accumulator (.d(alu__out), .enable(load__acc), .reset(reset), .clk(clk), .q(accum));
  four_bit_mux accum__mux (.a(data__mux_y), .b(accum), .sel(acc__to__db), .y(data__bus));
  program_ram program_ram_1 (
    .addr(addr__bus), .data__in(data__bus), .clk(clk), .write(write), .data__out(program_ram_1_data__out));
  four_bit_mux data__mux (.a(data__in), .b(program_ram_1_data__out), .sel(read), .y(data__mux_y));
endmodule
