// Digital circuit four_bit_reg.dig as structural Verilog
module four_bit_reg (
  input  [3:0] d,
  input  enable,
  input  reset,
  input  clk,
  output [3:0] q
);

  wire [3:0] four_bit_mux_1_y;

  four_bit_mux four_bit_mux_1 (.a(q), .b(d), .sel(enable), .y(four_bit_mux_1_y));
  D_FF_AS d_ff_as_1 (.Set(1'b0), .D(four_bit_mux_1_y[3]), .C(clk), .Clr(reset), .Q(q[3]));  // open: nQ
  D_FF_AS d_ff_as_2 (.Set(1'b0), .D(four_bit_mux_1_y[2]), .C(clk), .Clr(reset), .Q(q[2]));  // open: nQ
  D_FF_AS d_ff_as_3 (.Set(1'b0), .D(four_bit_mux_1_y[1]), .C(clk), .Clr(reset), .Q(q[1]));  // open: nQ
  D_FF_AS d_ff_as_4 (.Set(1'b0), .D(four_bit_mux_1_y[0]), .C(clk), .Clr(reset), .Q(q[0]));  // open: nQ
endmodule
