// Digital circuit 4byteALU.dig as structural Verilog
module _4byteALU (
  input  [31:0] a,
  input  [31:0] b,
  input  [1:0] op,
  input  Bnegative,
  input  AInvert,
  output zero,
  output [31:0] y,
  output cout,
  output overfl
);

  wire alu_1_cout, alu_2_cout, alu_3_cout, alu_4_cout, alu_5_cout, alu_6_cout, alu_7_cout, alu_8_cout,
       alu_9_cout, alu_10_cout, alu_11_cout, alu_12_cout, alu_13_cout, alu_14_cout, alu_15_cout, alu_16_cout,
       alu_17_cout, alu_18_cout, alu_19_cout, alu_20_cout, alu_21_cout, alu_22_cout, alu_23_cout,
       alu_24_cout, alu_25_cout, alu_26_cout, alu_27_cout, alu_28_cout, alu_29_cout, alu_30_cout,
       alu_31_cout, alu_32_set, and_1_out, and_3_out, nor_1_out, nor_2_out, nor_3_out, nor_4_out, nor_5_out,
       nor_6_out, nor_7_out, nor_8_out;

  ALU alu_1 (
    .a(a[0]), .b(b[0]), .Ainvert(AInvert), .Binvert(Bnegative), .cin(Bnegative), .less(alu_32_set), .op(op),
    .y(y[0]), .cout(alu_1_cout));  // open: overfl, set
  ALU alu_2 (
    .a(a[1]), .b(b[1]), .Ainvert(AInvert), .Binvert(Bnegative), .cin(alu_1_cout), .less(1'b0), .op(op),
    .y(y[1]), .cout(alu_2_cout));  // open: overfl, set
  ALU alu_3 (
    .a(a[2]), .b(b[2]), .Ainvert(AInvert), .Binvert(Bnegative), .cin(alu_2_cout), .less(1'b0), .op(op),
    .y(y[2]), .cout(alu_3_cout));  // open: overfl, set
  ALU alu_4 (
    .a(a[3]), .b(b[3]), .Ainvert(AInvert), .Binvert(Bnegative), .cin(alu_3_cout), .less(1'b0), .op(op),
    .y(y[3]), .cout(alu_4_cout));  // open: overfl, set
  ALU alu_5 (
    .a(a[4]), .b(b[4]), .Ainvert(AInvert), .Binvert(Bnegative), .cin(alu_28_cout), .less(1'b0), .op(op),
    .y(y[4]), .cout(alu_5_cout));  // open: overfl, set
  ALU alu_6 (
    .a(a[5]), .b(b[5]), .Ainvert(AInvert), .Binvert(Bnegative), .cin(alu_5_cout), .less(1'b0), .op(op),
    .y(y[5]), .cout(alu_6_cout));  // open: overfl, set
  ALU alu_7 (
    .a(a[6]), .b(b[6]), .Ainvert(AInvert), .Binvert(Bnegative), .cin(alu_6_cout), .less(1'b0), .op(op),
    .y(y[6]), .cout(alu_7_cout));  // open: overfl, set
  ALU alu_8 (
    .a(a[7]), .b(b[7]), .Ainvert(AInvert), .Binvert(Bnegative), .cin(alu_7_cout), .less(1'b0), .op(op),
    .y(y[7]), .cout(alu_8_cout));  // open: overfl, set
  nor nor_1 (nor_1_out, y[0], y[1], y[2], y[3]);
  nor nor_2 (nor_2_out, y[4], y[5], y[6], y[7]);
  ALU alu_9 (
    .a(a[8]), .b(b[8]), .Ainvert(AInvert), .Binvert(Bnegative), .cin(alu_4_cout), .less(1'b0), .op(op),
    .y(y[8]), .cout(alu_9_cout));  // open: overfl, set
  ALU alu_10 (
    .a(a[9]), .b(b[9]), .Ainvert(AInvert), .Binvert(Bnegative), .cin(alu_9_cout), .less(1'b0), .op(op),
    .y(y[9]), .cout(alu_10_cout));  // open: overfl, set
  ALU alu_11 (
    .a(a[10]), .b(b[10]), .Ainvert(AInvert), .Binvert(Bnegative), .cin(alu_10_cout), .less(1'b0), .op(op),
    .y(y[10]), .cout(alu_11_cout));  // open: overfl, set
  ALU alu_12 (
    .a(a[11]), .b(b[11]), .Ainvert(AInvert), .Binvert(Bnegative), .cin(alu_11_cout), .less(1'b0), .op(op),
    .y(y[11]), .cout(alu_12_cout));  // open: overfl, set
  ALU alu_13 (
    .a(a[12]), .b(b[12]), .Ainvert(AInvert), .Binvert(Bnegative), .cin(alu_8_cout), .less(1'b0), .op(op),
    .y(y[12]), .cout(alu_13_cout));  // open: overfl, set
  ALU alu_14 (
    .a(a[13]), .b(b[13]), .Ainvert(AInvert), .Binvert(Bnegative), .cin(alu_13_cout), .less(1'b0), .op(op),
    .y(y[13]), .cout(alu_14_cout));  // open: overfl, set
  ALU alu_15 (
    .a(a[14]), .b(b[14]), .Ainvert(AInvert), .Binvert(Bnegative), .cin(alu_14_cout), .less(1'b0), .op(op),
    .y(y[14]), .cout(alu_15_cout));  // open: overfl, set
  ALU alu_16 (
    .a(a[15]), .b(b[15]), .Ainvert(AInvert), .Binvert(Bnegative), .cin(alu_15_cout), .less(1'b0), .op(op),
    .y(y[15]), .cout(alu_16_cout));  // open: overfl, set
  nor nor_3 (nor_3_out, y[8], y[9], y[10], y[11]);
  nor nor_4 (nor_4_out, y[14], y[15], y[12], y[15]);
  ALU alu_17 (
    .a(a[16]), .b(b[16]), .Ainvert(AInvert), .Binvert(Bnegative), .cin(alu_12_cout), .less(1'b0), .op(op),
    .y(y[16]), .cout(alu_17_cout));  // open: overfl, set
  ALU alu_18 (
    .a(a[17]), .b(b[17]), .Ainvert(AInvert), .Binvert(Bnegative), .cin(alu_17_cout), .less(1'b0), .op(op),
    .y(y[17]), .cout(alu_18_cout));  // open: overfl, set
  ALU alu_19 (
    .a(a[18]), .b(b[18]), .Ainvert(AInvert), .Binvert(Bnegative), .cin(alu_18_cout), .less(1'b0), .op(op),
    .y(y[18]), .cout(alu_19_cout));  // open: overfl, set
  ALU alu_20 (
    .a(a[19]), .b(b[19]), .Ainvert(AInvert), .Binvert(Bnegative), .cin(alu_19_cout), .less(1'b0), .op(op),
    .y(y[19]), .cout(alu_20_cout));  // open: overfl, set
  ALU alu_21 (
    .a(a[20]), .b(b[20]), .Ainvert(AInvert), .Binvert(Bnegative), .cin(alu_16_cout), .less(1'b0), .op(op),
    .y(y[20]), .cout(alu_21_cout));  // open: overfl, set
  ALU alu_22 (
    .a(a[21]), .b(b[21]), .Ainvert(AInvert), .Binvert(Bnegative), .cin(alu_21_cout), .less(1'b0), .op(op),
    .y(y[21]), .cout(alu_22_cout));  // open: overfl, set
  ALU alu_23 (
    .a(a[22]), .b(b[22]), .Ainvert(AInvert), .Binvert(Bnegative), .cin(alu_22_cout), .less(1'b0), .op(op),
    .y(y[22]), .cout(alu_23_cout));  // open: overfl, set
  ALU alu_24 (
    .a(a[23]), .b(b[23]), .Ainvert(AInvert), .Binvert(Bnegative), .cin(alu_23_cout), .less(1'b0), .op(op),
    .y(y[23]), .cout(alu_24_cout));  // open: overfl, set
  nor nor_5 (nor_5_out, y[16], y[17], y[18], y[19]);
  nor nor_6 (nor_6_out, y[20], y[22], y[20], y[23]);
  ALU alu_25 (
    .a(a[24]), .b(b[24]), .Ainvert(AInvert), .Binvert(Bnegative), .cin(alu_20_cout), .less(1'b0), .op(op),
    .y(y[24]), .cout(alu_25_cout));  // open: overfl, set
  ALU alu_26 (
    .a(a[25]), .b(b[25]), .Ainvert(AInvert), .Binvert(Bnegative), .cin(alu_25_cout), .less(1'b0), .op(op),
    .y(y[25]), .cout(alu_26_cout));  // open: overfl, set
  ALU alu_27 (
    .a(a[26]), .b(b[26]), .Ainvert(AInvert), .Binvert(Bnegative), .cin(alu_26_cout), .less(1'b0), .op(op),
    .y(y[26]), .cout(alu_27_cout));  // open: overfl, set
  ALU alu_28 (
    .a(a[27]), .b(b[27]), .Ainvert(AInvert), .Binvert(Bnegative), .cin(alu_27_cout), .less(1'b0), .op(op),
    .y(y[27]), .cout(alu_28_cout));  // open: overfl, set
  ALU alu_29 (
    .a(a[28]), .b(b[28]), .Ainvert(AInvert), .Binvert(Bnegative), .cin(alu_24_cout), .less(1'b0), .op(op),
    .y(y[28]), .cout(alu_29_cout));  // open: overfl, set
  ALU alu_30 (
    .a(a[29]), .b(b[29]), .Ainvert(AInvert), .Binvert(Bnegative), .cin(alu_29_cout), .less(1'b0), .op(op),
    .y(y[29]), .cout(alu_30_cout));  // open: overfl, set
  ALU alu_31 (
    .a(a[30]), .b(b[30]), .Ainvert(AInvert), .Binvert(Bnegative), .cin(alu_30_cout), .less(1'b0), .op(op),
    .y(y[30]), .cout(alu_31_cout));  // open: overfl, set
  ALU alu_32 (
    .a(a[31]), .b(b[31]), .Ainvert(AInvert), .Binvert(Bnegative), .cin(alu_31_cout), .less(1'b0), .op(op),
    .y(y[31]), .cout(cout), .overfl(overfl), .set(alu_32_set));
  nor nor_7 (nor_7_out, y[24], y[25], y[26], y[27]);
  nor nor_8 (nor_8_out, y[30], y[29], y[28], y[31]);
  and and_1 (and_1_out, nor_3_out, nor_1_out, nor_5_out, nor_7_out);
  and and_2 (zero, and_1_out, and_3_out);
  and and_3 (and_3_out, nor_8_out, nor_6_out, nor_4_out, nor_2_out);
endmodule
