// Digital circuit 4byteAdder.dig as structural Verilog
module _4byteAdder (
  input  [31:0] a,
  input  [31:0] b,
  input  cin,
  output [31:0] y,
  output cout,
  output overfl
);

  wire _8bit_adder_1_cout, _8bit_adder_2_cout, _8bit_adder_3_cout;

  _8bit_adder _8bit_adder_1 (.a(a[7:0]), .b(b[7:0]), .cin(cin), .y(y[7:0]), .cout(_8bit_adder_1_cout));  // open: overfl
  _8bit_adder _8bit_adder_2 (
    .a(a[15:8]), .b(b[15:8]), .cin(_8bit_adder_1_cout), .y(y[15:8]), .cout(_8bit_adder_2_cout));  // open: overfl
  _8bit_adder _8bit_adder_3 (
    .a(a[23:16]), .b(b[23:16]), .cin(_8bit_adder_2_cout), .y(y[23:16]), .cout(_8bit_adder_3_cout));  // open: overfl
  _8bit_adder _8bit_adder_4 (
    .a(a[31:24]), .b(b[31:24]), .cin(_8bit_adder_3_cout), .y(y[31:24]), .cout(cout), .overfl(overfl));
endmodule
