// Digital circuit 4byteMux.dig as structural Verilog
module _4byteMux (
  input  [31:0] a,
  input  [31:0] b,
  input  s,
  output [31:0] y
);

  _8bit_mux _8bit_mux_1 (.a(a[7:0]), .b(b[7:0]), .s(s), .y(y[7:0]));
  _8bit_mux _8bit_mux_2 (.a(a[15:8]), .b(b[15:8]), .s(s), .y(y[15:8]));
  _8bit_mux _8bit_mux_3 (.a(a[23:16]), .b(b[23:16]), .s(s), .y(y[23:16]));
  _8bit_mux _8bit_mux_4 (.a(a[31:24]), .b(b[31:24]), .s(s), .y(y[31:24]));
endmodule
