// Digital circuit 4byteReg.dig as structural Verilog
module _4byteReg (
  input  [31:0] d,
  input  enable,
  input  reset,
  input  clk,
  output [31:0] q
);

  _8bit_reg _8bit_reg_1 (.d(d[7:0]), .enable(enable), .reset(reset), .clk(clk), .q(q[7:0]));
  _8bit_reg _8bit_reg_2 (.d(d[15:8]), .enable(enable), .reset(reset), .clk(clk), .q(q[15:8]));
  _8bit_reg _8bit_reg_3 (.d(d[23:16]), .enable(enable), .reset(reset), .clk(clk), .q(q[23:16]));
  _8bit_reg _8bit_reg_4 (.d(d[31:24]), .enable(enable), .reset(reset), .clk(clk), .q(q[31:24]));
endmodule
