// Digital circuit 5bitMux.dig as structural Verilog
module _5bitMux (
  input  [4:0] a,
  input  [4:0] b,
  input  s,
  output [4:0] y
);

  wire and_1_out, and_2_out, and_3_out, and_4_out, and_5_out, and_6_out, and_7_out, and_8_out, and_9_out,
       and_10_out;

  and and_1 (and_1_out, a[0], ~s);  // And
  and and_2 (and_2_out, s, b[0]);
  and and_3 (and_3_out, a[1], ~s);  // And
  and and_4 (and_4_out, s, b[1]);
  and and_5 (and_5_out, a[2], ~s);  // And
  and and_6 (and_6_out, s, b[2]);
  or or_1 (y[0], and_1_out, and_2_out);
  or or_2 (y[1], and_3_out, and_4_out);
  or or_3 (y[2], and_5_out, and_6_out);
  and and_7 (and_7_out, a[3], ~s);  // And
  and and_8 (and_8_out, s, b[3]);
  and and_9 (and_9_out, a[4], ~s);  // And
  and and_10 (and_10_out, s, b[4]);
  or or_4 (y[3], and_7_out, and_8_out);
  or or_5 (y[4], and_9_out, and_10_out);
endmodule
