// Digital circuit 8bit_adder.dig as structural Verilog
module _8bit_adder (
  input  [7:0] a,
  input  [7:0] b,
  input  cin,
  output [7:0] y,
  output cout,
  output overfl
);

  wire and_1_out, and_2_out, and_3_out, and_4_out, and_5_out, and_6_out, and_7_out, and_8_out, and_9_out,
       and_10_out, and_11_out, and_12_out, and_13_out, and_14_out, and_15_out, and_16_out, and_17_out,
       and_18_out, and_19_out, and_20_out, and_21_out, and_22_out, and_23_out, and_24_out, or_2_out,
       or_3_out, or_4_out, or_5_out, or_6_out, or_7_out, or_8_out;

  xor xor_1 (y[7], a[7], b[7], or_2_out);
  and and_1 (and_1_out, or_2_out, a[7]);
  and and_2 (and_2_out, or_2_out, b[7]);
  and and_3 (and_3_out, b[7], a[7]);
  xor xor_2 (y[6], a[6], b[6], or_3_out);
  and and_4 (and_4_out, or_3_out, a[6]);
  and and_5 (and_5_out, or_3_out, b[6]);
  and and_6 (and_6_out, b[6], a[6]);
  xor xor_3 (y[5], a[5], b[5], or_4_out);
  and and_7 (and_7_out, or_4_out, a[5]);
  and and_8 (and_8_out, or_4_out, b[5]);
  and and_9 (and_9_out, b[5], a[5]);
  xor xor_4 (y[4], a[4], b[4], or_5_out);
  and and_10 (and_10_out, or_5_out, a[4]);
  and and_11 (and_11_out, or_5_out, b[4]);
  and and_12 (and_12_out, b[4], a[4]);
  xor xor_5 (y[3], a[3], b[3], or_6_out);
  and and_13 (and_13_out, or_6_out, a[3]);
  and and_14 (and_14_out, or_6_out, b[3]);
  and and_15 (and_15_out, b[3], a[3]);
  xor xor_6 (y[2], a[2], b[2], or_7_out);
  and and_16 (and_16_out, or_7_out, a[2]);
  and and_17 (and_17_out, or_7_out, b[2]);
  and and_18 (and_18_out, b[2], a[2]);
  xor xor_7 (y[1], a[1], b[1], or_8_out);
  and and_19 (and_19_out, or_8_out, a[1]);
  and and_20 (and_20_out, or_8_out, b[1]);
  and and_21 (and_21_out, b[1], a[1]);
  xor xor_8 (y[0], a[0], b[0], cin);
  and and_22 (and_22_out, cin, a[0]);
  and and_23 (and_23_out, cin, b[0]);
  and and_24 (and_24_out, b[0], a[0]);
  or or_1 (cout, and_1_out, and_2_out, and_3_out);
  or or_2 (or_2_out, and_4_out, and_5_out, and_6_out);
  or or_3 (or_3_out, and_7_out, and_8_out, and_9_out);
  or or_4 (or_4_out, and_10_out, and_11_out, and_12_out);
  or or_5 (or_5_out, and_13_out, and_14_out, and_15_out);
  or or_6 (or_6_out, and_16_out, and_17_out, and_18_out);
  or or_7 (or_7_out, and_19_out, and_20_out, and_21_out);
  or or_8 (or_8_out, and_22_out, and_23_out, and_24_out);
  xor xor_9 (overfl, cout, or_2_out);
endmodule
