// Digital circuit 8bit_mux.dig as structural Verilog
module _8bit_mux (
  input  [7:0] a,
  input  [7:0] b,
  input  s,
  output [7:0] y
);

  wire and_1_out, and_2_out, and_3_out, and_4_out, and_5_out, and_6_out, and_7_out, and_8_out, and_9_out,
       and_10_out, and_11_out, and_12_out, and_13_out, and_14_out, and_15_out, and_16_out;

  and and_1 (and_1_out, a[0], ~s);  // And
  and and_2 (and_2_out, b[0], s);
  and and_3 (and_3_out, a[1], ~s);  // And
  and and_4 (and_4_out, b[1], s);
  and and_5 (and_5_out, a[2], ~s);  // And
  and and_6 (and_6_out, b[2], s);
  and and_7 (and_7_out, a[3], ~s);  // And
  and and_8 (and_8_out, b[3], s);
  and and_9 (and_9_out, a[4], ~s);  // And
  and and_10 (and_10_out, b[4], s);
  and and_11 (and_11_out, a[5], ~s);  // And
  and and_12 (and_12_out, b[5], s);
  and and_13 (and_13_out, a[6], ~s);  // And
  and and_14 (and_14_out, b[6], s);
  and and_15 (and_15_out, a[7], ~s);  // And
  and and_16 (and_16_out, b[7], s);
  or or_1 (y[0], and_1_out, and_2_out);
  or or_2 (y[1], and_3_out, and_4_out);
  or or_3 (y[2], and_5_out, and_6_out);
  or or_4 (y[3], and_7_out, and_8_out);
  or or_5 (y[4], and_9_out, and_10_out);
  or or_6 (y[5], and_11_out, and_12_out);
  or or_7 (y[6], and_13_out, and_14_out);
  or or_8 (y[7], and_15_out, and_16_out);
endmodule
