// Digital circuit 8bit_reg.dig as structural Verilog
module _8bit_reg (
  input  [7:0] d,
  input  enable,
  input  reset,
  input  clk,
  output [7:0] q
);

  wire [7:0] _8bit_mux_1_y;

  _8bit_mux _8bit_mux_1 (.a(q), .b(d), .s(enable), .y(_8bit_mux_1_y));
  D_FF_AS d_ff_as_1 (.Set(1'b0), .D(_8bit_mux_1_y[7]), .C(clk), .Clr(reset), .Q(q[7]));  // open: nQ
  D_FF_AS d_ff_as_2 (.Set(1'b0), .D(_8bit_mux_1_y[6]), .C(clk), .Clr(reset), .Q(q[6]));  // open: nQ
  D_FF_AS d_ff_as_3 (.Set(1'b0), .D(_8bit_mux_1_y[5]), .C(clk), .Clr(reset), .Q(q[5]));  // open: nQ
  D_FF_AS d_ff_as_4 (.Set(1'b0), .D(_8bit_mux_1_y[4]), .C(clk), .Clr(reset), .Q(q[4]));  // open: nQ
  D_FF_AS d_ff_as_5 (.Set(1'b0), .D(_8bit_mux_1_y[3]), .C(clk), .Clr(reset), .Q(q[3]));  // open: nQ
  D_FF_AS d_ff_as_6 (.Set(1'b0), .D(_8bit_mux_1_y[2]), .C(clk), .Clr(reset), .Q(q[2]));  // open: nQ
  D_FF_AS d_ff_as_7 (.Set(1'b0), .D(_8bit_mux_1_y[1]), .C(clk), .Clr(reset), .Q(q[1]));  // open: nQ
  D_FF_AS d_ff_as_8 (.Set(1'b0), .D(_8bit_mux_1_y[0]), .C(clk), .Clr(reset), .Q(q[0]));  // open: nQ
endmodule
