// Digital circuit ALU.dig as structural Verilog
module ALU (
  input  a,
  input  b,
  input  Ainvert,
  input  Binvert,
  input  cin,
  input  less,
  input  [1:0] op,
  output y,
  output cout,
  output overfl,
  output set
);

  wire and_1_out, and_2_out, and_3_out, and_4_out, and_5_out, and_6_out, and_7_out, and_8_out, and_9_out,
       and_10_out, and_11_out, and_12_out, and_13_out, and_14_out, not_1_out, not_2_out, or_1_out, or_2_out,
       or_3_out, or_5_out, or_6_out;

  not not_1 (not_1_out, a);
  not not_2 (not_2_out, b);
  and and_1 (and_1_out, a, ~Ainvert);  // And
  and and_2 (and_2_out, not_1_out, Ainvert);
  and and_3 (and_3_out, b, ~Binvert);  // And
  and and_4 (and_4_out, not_2_out, Binvert);
  or or_1 (or_1_out, and_1_out, and_2_out);
  or or_2 (or_2_out, and_3_out, and_4_out);
  and and_5 (and_5_out, cin, or_2_out);
  and and_6 (and_6_out, cin, or_1_out);
  and and_7 (and_7_out, or_2_out, or_1_out);
  and and_8 (and_8_out, or_1_out, or_2_out);
  or or_3 (or_3_out, or_1_out, or_2_out);
  xor xor_1 (set, or_1_out, cin, or_2_out);
  or or_4 (cout, and_5_out, and_6_out, and_7_out);
  xor xor_2 (overfl, cin, cout);
  and and_9 (and_9_out, and_8_out, ~op[0]);  // And
  and and_10 (and_10_out, or_3_out, op[0]);
  and and_11 (and_11_out, set, ~op[0]);  // And
  and and_12 (and_12_out, less, op[0]);
  or or_5 (or_5_out, and_9_out, and_10_out);
  or or_6 (or_6_out, and_11_out, and_12_out);
  and and_13 (and_13_out, or_5_out, ~op[1]);  // And
  and and_14 (and_14_out, or_6_out, op[1]);
  or or_7 (y, and_13_out, and_14_out);
endmodule
