// Digital circuit ALUControl.dig as structural Verilog
module ALUControl (
  input  [5:0] func,
  input  [1:0] ALUOp,
  output [3:0] ctrl
);

  wire and_1_out, and_2_out, and_3_out, and_4_out, and_5_out, and_6_out, and_7_out, and_8_out, and_9_out,
       nor_1_out;
  wire [3:0] rom_1_d;

  nor nor_1 (nor_1_out, ALUOp[0], ~ALUOp[1]);  // NOr
  and and_1 (and_1_out, ~ALUOp[0], ALUOp[1]);  // And
  ROM #(.AddrBits(6), .Bits(4)) rom_1 (.A(func), .sel(nor_1_out), .D(rom_1_d));
  and and_2 (and_2_out, rom_1_d[0], and_1_out);
  and and_3 (and_3_out, ~and_1_out, 1'b0);  // And
  and and_4 (and_4_out, rom_1_d[1], and_1_out);
  and and_5 (and_5_out, ~and_1_out, 1'b1);  // And
  and and_6 (and_6_out, rom_1_d[2], and_1_out);
  and and_7 (and_7_out, ~and_1_out, ALUOp[0]);  // And
  and and_8 (and_8_out, rom_1_d[3], and_1_out);
  and and_9 (and_9_out, ~and_1_out, 1'b0);  // And
  or or_1 (ctrl[0], and_2_out, and_3_out);
  or or_2 (ctrl[1], and_4_out, and_5_out);
  or or_3 (ctrl[2], and_6_out, and_7_out);
  or or_4 (ctrl[3], and_8_out, and_9_out);

  // Notes on the sheet:
  //   rom_1 loads aluctrl_rom.hex
endmodule
