// Digital circuit testing.dig as structural Verilog
module testing (
  input  clk,
  input  pc__rst,
  output [31:0] alu__y
);

  wire _4bytealu_1_zero, and_1_out;
  wire [1:0] control_d;
  wire [3:0] alucontrol_1_ctrl;
  wire [4:0] Instructions_d_3, Instructions_d_4, Instructions_d_5, RegDst_y;
  wire [5:0] Instructions_d;
  wire [9:2] control_d_2;
  wire [31:0] _4byteadder_1_y, _4byteadder_2_y, ALUSrc_y, bitextender_1_out, branch_y, Data_d, Jump_y,
       memtoreg_y, PC_q, registerfile_1_da, registerfile_1_db;
  wire [31:6] Instructions_d_2;

  _4byteReg PC (.d(Jump_y), .enable(1'b1), .reset(pc__rst), .clk(clk), .q(PC_q));
  _4byteAdder _4byteadder_1 (.a(32'h1), .b(PC_q), .cin(1'b0), .y(_4byteadder_1_y));  // open: cout, overfl
  ROM #(.AddrBits(24), .Bits(32)) Instructions (
    .A(PC_q[23:0]), .sel(1'b1),
    .D({Instructions_d_2[31:26], Instructions_d_5, Instructions_d_4, Instructions_d_3, Instructions_d_2[10:6], Instructions_d}));
  BitExtender #(.inputBits(16), .outputBits(32)) bitextender_1 (
    .in({Instructions_d_3, Instructions_d_2[10:6], Instructions_d}), .out(bitextender_1_out));
  ROM #(.AddrBits(6), .Bits(10)) control (.A(Instructions_d_2[31:26]), .sel(1'b1), .D({control_d_2, control_d}));
  _4byteMux Jump (
    .a(branch_y),
    .b({_4byteadder_1_y[31:26], Instructions_d_5, Instructions_d_4, Instructions_d_3, Instructions_d_2[10:6], Instructions_d}),
    .s(control_d_2[9]), .y(Jump_y));
  _5bitMux RegDst (.a(Instructions_d_4), .b(Instructions_d_3), .s(control_d_2[8]), .y(RegDst_y));
  _4byteAdder _4byteadder_2 (
    .a(_4byteadder_1_y), .b(bitextender_1_out), .cin(1'b0), .y(_4byteadder_2_y));  // open: cout, overfl
  RegisterFile #(.AddrBits(5), .Bits(32)) registerfile_1 (
    .Din(memtoreg_y), .we(control_d_2[5]), .Rw(RegDst_y), .C(clk), .Ra(Instructions_d_5),
    .Rb(Instructions_d_4), .Da(registerfile_1_da), .Db(registerfile_1_db));
  ALUControl alucontrol_1 (.func(Instructions_d), .ALUOp(control_d), .ctrl(alucontrol_1_ctrl));
  _4byteMux ALUSrc (.a(registerfile_1_db), .b(bitextender_1_out), .s(control_d_2[7]), .y(ALUSrc_y));
  and and_1 (and_1_out, control_d_2[2], _4bytealu_1_zero);
  _4byteALU _4bytealu_1 (
    .a(registerfile_1_da), .b(ALUSrc_y), .op(alucontrol_1_ctrl[1:0]), .Bnegative(alucontrol_1_ctrl[2]),
    .AInvert(alucontrol_1_ctrl[3]), .zero(_4bytealu_1_zero), .y(alu__y));  // open: cout, overfl
  _4byteMux branch (.a(_4byteadder_1_y), .b(_4byteadder_2_y), .s(and_1_out), .y(branch_y));
  _4byteMux memtoreg (.a(alu__y), .b(Data_d), .s(control_d_2[6]), .y(memtoreg_y));
  RAMDualPort #(.AddrBits(24), .isProgramMemory("true"), .Bits(32)) Data (
    .A(alu__y[23:0]), .Din(registerfile_1_db), .str(control_d_2[3]), .C(clk), .ld(control_d_2[4]), .D(Data_d));

  // Notes on the sheet:
  //   Instructions loads instructionMem.hex
  //   control loads control_rom.hex
endmodule
